// Logisim project comparador.circ as structural Verilog: 1 circuit, main circuit main
module main (
  input  in_1,
  input  in_2,
  input  in_3,
  input  in_4,
  input  in_5,
  input  in_6,
  input  in_7,
  input  in_8,
  output out_9,
  output out_10,
  output out_11,
  output out_12,
  output out_13,
  output out_14,
  output out_15,
  output out_16
);

  wire and_3_out, and_4_out, and_5_out, and_6_out, and_7_out, and_8_out, and_15_out, and_16_out, nor_1_out,
       nor_2_out, nor_3_out, not_1_out, not_2_out, not_3_out, not_4_out, not_5_out, not_6_out, not_7_out,
       not_8_out;

  not not_1 (not_1_out, in_1);
  not not_2 (not_2_out, in_2);
  not not_3 (not_3_out, in_3);
  not not_4 (not_4_out, in_4);
  not not_5 (not_5_out, in_5);
  not not_6 (not_6_out, in_6);
  not not_7 (not_7_out, in_7);
  not not_8 (not_8_out, in_8);
  and and_1 (out_9, not_1_out, in_2);
  and and_2 (out_10, in_1, not_2_out);
  and and_3 (and_3_out, not_3_out, in_4);
  and and_4 (and_4_out, in_3, not_4_out);
  and and_5 (and_5_out, not_5_out, in_6);
  and and_6 (and_6_out, in_5, not_6_out);
  and and_7 (and_7_out, not_7_out, in_8);
  and and_8 (and_8_out, in_7, not_8_out);
  and and_9 (out_11, nor_1_out, and_3_out);
  and and_10 (out_12, nor_1_out, and_4_out);
  and and_11 (out_13, and_15_out, and_5_out);
  and and_12 (out_14, and_15_out, and_6_out);
  and and_13 (out_15, and_16_out, and_7_out);
  and and_14 (out_16, and_16_out, and_8_out);
  nor nor_1 (nor_1_out, out_9, out_10);
  and and_15 (and_15_out, nor_1_out, nor_2_out);
  nor nor_2 (nor_2_out, out_11, out_12);
  and and_16 (and_16_out, and_15_out, nor_3_out);
  nor nor_3 (nor_3_out, out_13, out_14);
endmodule
